// Digital circuit 8位加法器.dig as structural Verilog
module \_8位加法器  (
  input  [7:0] in_1,
  input  [7:0] in_2,
  output [7:0] C,
  output Carry
);

  wire \全加器_1_carry , \全加器_2_carry , \全加器_3_carry , \全加器_4_carry , \全加器_5_carry , \全加器_6_carry ,
       \半加器_1_carry ;

  \半加器  \u_半加器_1  (.A(in_1[0]), .B(in_2[0]), .SUM(C[0]), .Carry(\半加器_1_carry ));
  \全加器  \u_全加器_1  (.C(\半加器_1_carry ), .A(in_1[1]), .B(in_2[1]), .SUM(C[1]), .Carry(\全加器_1_carry ));
  \全加器  \u_全加器_2  (.C(\全加器_1_carry ), .A(in_1[2]), .B(in_2[2]), .SUM(C[2]), .Carry(\全加器_2_carry ));
  \全加器  \u_全加器_3  (.C(\全加器_2_carry ), .A(in_1[3]), .B(in_2[3]), .SUM(C[3]), .Carry(\全加器_3_carry ));
  \全加器  \u_全加器_4  (.C(\全加器_3_carry ), .A(in_1[4]), .B(in_2[4]), .SUM(C[4]), .Carry(\全加器_4_carry ));
  \全加器  \u_全加器_5  (.C(\全加器_4_carry ), .A(in_1[5]), .B(in_2[5]), .SUM(C[5]), .Carry(\全加器_5_carry ));
  \全加器  \u_全加器_6  (.C(\全加器_5_carry ), .A(in_1[6]), .B(in_2[6]), .SUM(C[6]), .Carry(\全加器_6_carry ));
  \全加器  \u_全加器_7  (.C(\全加器_6_carry ), .A(in_1[7]), .B(in_2[7]), .SUM(C[7]), .Carry(Carry));
endmodule
