// Digital circuit 16位存储器.dig as structural Verilog
module \_16位存储器  (
  input  Din,
  input  str,
  input  ld,
  input  [3:0] in_4,
  output Dout
);

  wire c0, c1, c2, c3, r0, r1, r2, r3;

  Decoder #(.Selector_Bits(2)) decoder_1 (.sel(in_4[1:0]), .out_0(c0), .out_1(c1), .out_2(c2), .out_3(c3));
  Decoder #(.Selector_Bits(2)) decoder_2 (.sel(in_4[3:2]), .out_0(r0), .out_1(r1), .out_2(r2), .out_3(r3));
  \最小内存单元memCell  \u_最小内存单元memcell_1  (.column(c0), .row(r0), .str(str), .din(Din), .ld(ld), .Dout(Dout));
  \最小内存单元memCell  \u_最小内存单元memcell_2  (.column(c0), .row(r1), .str(str), .din(Din), .ld(ld), .Dout(Dout));
  \最小内存单元memCell  \u_最小内存单元memcell_3  (.column(c0), .row(r2), .str(str), .din(Din), .ld(ld), .Dout(Dout));
  \最小内存单元memCell  \u_最小内存单元memcell_4  (.column(c0), .row(r3), .str(str), .din(Din), .ld(ld), .Dout(Dout));
  \最小内存单元memCell  \u_最小内存单元memcell_5  (.column(c1), .row(r0), .str(str), .din(Din), .ld(ld), .Dout(Dout));
  \最小内存单元memCell  \u_最小内存单元memcell_6  (.column(c1), .row(r1), .str(str), .din(Din), .ld(ld), .Dout(Dout));
  \最小内存单元memCell  \u_最小内存单元memcell_7  (.column(c1), .row(r2), .str(str), .din(Din), .ld(ld), .Dout(Dout));
  \最小内存单元memCell  \u_最小内存单元memcell_8  (.column(c1), .row(r3), .str(str), .din(Din), .ld(ld), .Dout(Dout));
  \最小内存单元memCell  \u_最小内存单元memcell_9  (.column(c2), .row(r0), .str(str), .din(Din), .ld(ld), .Dout(Dout));
  \最小内存单元memCell  \u_最小内存单元memcell_10  (.column(c2), .row(r1), .str(str), .din(Din), .ld(ld), .Dout(Dout));
  \最小内存单元memCell  \u_最小内存单元memcell_11  (.column(c2), .row(r2), .str(str), .din(Din), .ld(ld), .Dout(Dout));
  \最小内存单元memCell  \u_最小内存单元memcell_12  (.column(c2), .row(r3), .str(str), .din(Din), .ld(ld), .Dout(Dout));
  \最小内存单元memCell  \u_最小内存单元memcell_13  (.column(c3), .row(r0), .str(str), .din(Din), .ld(ld), .Dout(Dout));
  \最小内存单元memCell  \u_最小内存单元memcell_14  (.column(c3), .row(r1), .str(str), .din(Din), .ld(ld), .Dout(Dout));
  \最小内存单元memCell  \u_最小内存单元memcell_15  (.column(c3), .row(r2), .str(str), .din(Din), .ld(ld), .Dout(Dout));
  \最小内存单元memCell  \u_最小内存单元memcell_16  (.column(c3), .row(r3), .str(str), .din(Din), .ld(ld), .Dout(Dout));
endmodule
