// Digital circuit 4位寄存器.dig as structural Verilog
module \_4位寄存器  (
  input  [3:0] Din,
  input  WE,
  input  OE,
  input  clock,
  output [3:0] Dout,
  output [3:0] Store_Data
);

  Register #(.Bits(4)) register_1 (.D(Din), .C(clock), .en(WE), .Q(Store_Data));
  assign Dout = OE ? Store_Data : 4'bz;  // Driver driver_1
endmodule
