// Digital circuit 8位寄存器.dig as structural Verilog
module \_8位寄存器  (
  input  [7:0] Din,
  input  WE,
  input  OE,
  input  clock,
  output [7:0] Dout,
  output [7:0] Store_Data
);

  Register #(.Bits(8)) register_1 (.D(Din), .C(clock), .en(WE), .Q(Store_Data));
  assign Dout = OE ? Store_Data : 8'bz;  // Driver driver_1
endmodule
