// Digital circuit 8位锁存1个字节.dig as structural Verilog
module \_8位锁存1个字节  (
  input  in_2,
  input  [7:0] in,
  output [7:0] out_1
);

  \锁存  \u_锁存_1  (.Din(in[0]), .WE(in_2), .out(out_1[0]));
  \锁存  \u_锁存_2  (.Din(in[1]), .WE(in_2), .out(out_1[1]));
  \锁存  \u_锁存_3  (.Din(in[2]), .WE(in_2), .out(out_1[2]));
  \锁存  \u_锁存_4  (.Din(in[3]), .WE(in_2), .out(out_1[3]));
  \锁存  \u_锁存_5  (.Din(in[4]), .WE(in_2), .out(out_1[4]));
  \锁存  \u_锁存_6  (.Din(in[5]), .WE(in_2), .out(out_1[5]));
  \锁存  \u_锁存_7  (.Din(in[6]), .WE(in_2), .out(out_1[6]));
  \锁存  \u_锁存_8  (.Din(in[7]), .WE(in_2), .out(out_1[7]));
endmodule
