// Digital circuit 下降沿锁存器.dig as structural Verilog
module \下降沿锁存器  (
  input  din,
  input  clock,
  output out
);

  wire \锁存_1_out , \非门_1_c ;

  \锁存  \u_锁存_1  (.Din(din), .WE(clock), .out(\锁存_1_out ));
  \非门  \u_非门_1  (.A(clock), .C(\非门_1_c ));
  \锁存  \u_锁存_2  (.Din(\锁存_1_out ), .WE(\非门_1_c ), .out(out));
endmodule
