// Digital circuit 最小内存单元memCell.dig as structural Verilog
module \最小内存单元memCell  (
  input  column,
  input  row,
  input  str,
  input  din,
  input  ld,
  output Dout
);

  wire \与门_1_c , \与门_2_c , \与门_3_c , \锁存_1_out ;

  \与门  \u_与门_1  (.A(column), .B(row), .C(\与门_1_c ));
  \与门  \u_与门_2  (.A(ld), .B(\与门_1_c ), .C(\与门_2_c ));
  \与门  \u_与门_3  (.A(str), .B(\与门_1_c ), .C(\与门_3_c ));
  \锁存  \u_锁存_1  (.Din(din), .WE(\与门_3_c ), .out(\锁存_1_out ));
  assign Dout = \与门_2_c  ? \锁存_1_out  : 1'bz;  // Driver driver_1
  PullDown pulldown_1 (.out(Dout));
endmodule
