// Digital circuit 全加器.dig as structural Verilog
module \全加器  (
  input  C,
  input  A,
  input  B,
  output SUM,
  output Carry
);

  wire \半加器_1_carry , \半加器_1_sum , \半加器_2_carry ;

  \半加器  \u_半加器_1  (.A(A), .B(B), .SUM(\半加器_1_sum ), .Carry(\半加器_1_carry ));
  \半加器  \u_半加器_2  (.A(C), .B(\半加器_1_sum ), .SUM(SUM), .Carry(\半加器_2_carry ));
  \异或门  \u_异或门_1  (.A(\半加器_2_carry ), .B(\半加器_1_carry ), .C(Carry));
endmodule
