// Digital circuit 异或门.dig as structural Verilog
module \异或门  (
  input  A,
  input  B,
  output C
);

  wire relaydt_1_p3, relaydt_1_p4;

  // RelayDT relaydt_1: pin names not known; wires that end beside it: A, 1'b1, relaydt_1_p3, relaydt_1_p4
  // RelayDT relaydt_2: pin names not known; wires that end beside it: 1'b0, B, relaydt_1_p4, relaydt_1_p3, 1'b0, C
  PullDown pulldown_1 (.out(C));
endmodule
