// Digital circuit 非门.dig as structural Verilog
module \非门  (
  input  A,
  output C
);

  // RelayDT relaydt_1: pin names not known; wires that end beside it: A, 1'b1, 1'b0, C
  PullDown pulldown_1 (.out(C));
endmodule
